// Logisim project Memory_Data_Logic.circ as structural Verilog: 1 circuit, main circuit Memory_Data_Logic
module Memory_Data_Logic (
  input  [7:0] valA_IN,
  input  [3:0] ICODE,
  output [7:0] ALU_A_OUT
);

  Multiplexer #(.select(4), .width(8), .enable("false")) multiplexer_1 (
    .in0({8{1'b0}}), .in1({8{1'b0}}), .in2({8{1'b0}}), .in3({8{1'b0}}), .in4({8{1'b0}}), .in5(valA_IN),
    .in6({8{1'b0}}), .in7({8{1'b0}}), .in8({8{1'b0}}), .in9({8{1'b0}}), .in10({8{1'b0}}), .in11(valA_IN),
    .in12({8{1'b0}}), .in14(valA_IN), .out(ALU_A_OUT), .sel(ICODE));  // open: in13, in15
endmodule
