// Logisim project _main.circ as structural Verilog: 6 circuits, main circuit main
module main (
);

  wire and_1_out, and_2_out, and_3_out, and_4_out, and_5_out, button_1_out, clock_1_out, clock_2_out,
       DECODE_ENABLE, EXECUTE_ENABLE, FETCH_ENABLE, memory_controller_1_write_enable, MEMORY_ENABLE,
       not_1_out, RAM_LOAD_ENABLE, RAM_STORE_ENABLE, reg_w_1_e_enable, reg_w_1_m_enable,
       register_read_logic_1_ra_enable, register_read_logic_1_rb_enable, rom_loader_1_ioenable,
       WRITEBACK_ENABLE;
  wire [1:0] alu_1_flag;
  wire [3:0] counter_1_q, instruction_memory_1_icode, instruction_memory_1_ifun, instruction_memory_1_ra,
       instruction_memory_1_rb, reg_read_sel_logic_1_r_b_out, reg_read_sel_logic_1_ra_out,
       reg_write_sel_dstem_1_dste, reg_write_sel_dstem_1_dstm;
  wire [7:0] adder_1_out, alu_1_alu_out, alu_a_logic_1_alu_a_out, instruction_memory_1_pc,
       instruction_memory_1_ramaddr_out, instruction_memory_1_valc, main_1_alu_b_out, mem_addr_1_addr_out,
       memory_data_logic_1_alu_a_out, n6x8_register_file_1_output_0, n6x8_register_file_1_output_1,
       pc_increment_jump_controller_1_pc_increment_final_output, RAM_ADDR, rom_loader_1_addrout,
       vala_valb_send_1_vala_out, vala_valb_send_1_valb_out, vale_send_1_vale_out, valm_send_1_valm_8_out;
  wire [23:0] bit_extender_1_out, RAM_DATA_IN, RAM_DATA_OUT, rom_loader_1_dataout, valm_send_1_valm_24_out;

  and and_1 (and_1_out, clock_1_out, not_1_out);
  Clock clock_1 (.out(clock_1_out));
  reg_w reg_w_1 (.iCODE_IN(instruction_memory_1_icode), .m_ENABLE(reg_w_1_m_enable), .e_ENABLE(reg_w_1_e_enable));
  Button button_1 (.out(button_1_out));
  Counter #(.width(4), .max('ha)) counter_1 (.Q(counter_1_q), .clk(and_1_out));  // open: load, D, count, carry, clr
  Decoder #(.select(4), .disabled(0)) decoder_1 (
    .out1(FETCH_ENABLE), .out3(DECODE_ENABLE), .out6(EXECUTE_ENABLE), .out8(MEMORY_ENABLE),
    .out10(WRITEBACK_ENABLE), .sel(counter_1_q), .en(not_1_out));  // open: out0, out2, out4, out5, out7, out9, out11, out12, out13, out14, out15
  not not_1 (not_1_out, rom_loader_1_ioenable);
  and and_2 (and_2_out, WRITEBACK_ENABLE, reg_w_1_m_enable);
  and and_3 (and_3_out, reg_w_1_e_enable, WRITEBACK_ENABLE);
  ROM_loader rom_loader_1 (
    .RELOAD(button_1_out), .DATAOUT(rom_loader_1_dataout), .ADDROUT(rom_loader_1_addrout),
    .IOENABLE(rom_loader_1_ioenable));
  // Probe on instruction_memory_1_ifun
  // Probe on RAM_ADDR
  // Probe on RAM_DATA_IN
  // Probe on instruction_memory_1_valc
  assign RAM_ADDR = FETCH_ENABLE ? instruction_memory_1_ramaddr_out : 8'bz;  // Controlled_Buffer controlled_buffer_1
  assign RAM_ADDR = rom_loader_1_ioenable ? rom_loader_1_addrout : 8'bz;  // Controlled_Buffer controlled_buffer_2
  assign RAM_DATA_IN = rom_loader_1_ioenable ? rom_loader_1_dataout : 24'bz;  // Controlled_Buffer controlled_buffer_3
  // Probe on reg_write_sel_dstem_1_dstm
  // Probe on reg_write_sel_dstem_1_dste
  instruction_memory instruction_memory_1 (
    .ENABLE(FETCH_ENABLE), .PC(instruction_memory_1_pc), .ICODE(instruction_memory_1_icode),
    .IFUN(instruction_memory_1_ifun), .rA(instruction_memory_1_ra), .rB(instruction_memory_1_rb),
    .valC(instruction_memory_1_valc), .NEWPC(pc_increment_jump_controller_1_pc_increment_final_output),
    .ramaddr_OUT(instruction_memory_1_ramaddr_out), .ramdata_IN(RAM_DATA_OUT));
  pc_increment_jump_controller pc_increment_jump_controller_1 (
    .PC_Increment_Final_Output(pc_increment_jump_controller_1_pc_increment_final_output), .FLAG(alu_1_flag),
    .ValC(instruction_memory_1_valc), .ifun(instruction_memory_1_ifun), .icode(instruction_memory_1_icode),
    .PC_Increment_Counter_Value(adder_1_out), .ValM(valm_send_1_valm_8_out));
  reg_write_sel_dstEM reg_write_sel_dstem_1 (
    .rA_IN(instruction_memory_1_ra), .rB_IN(instruction_memory_1_rb), .icode_IN(instruction_memory_1_icode),
    .dstM(reg_write_sel_dstem_1_dstm), .dstE(reg_write_sel_dstem_1_dste));
  Adder adder_1 (.a(instruction_memory_1_pc), .b(8'h1), .out(adder_1_out));  // open: cin, cout
  // Probe on alu_a_logic_1_alu_a_out
  // Probe on pc_increment_jump_controller_1_pc_increment_final_output
  assign RAM_ADDR = MEMORY_ENABLE ? mem_addr_1_addr_out : 8'bz;  // Controlled_Buffer controlled_buffer_4
  mem_addr mem_addr_1 (
    .valA_IN(vala_valb_send_1_vala_out), .valE_IN(vale_send_1_vale_out), .ICODE(instruction_memory_1_icode),
    .Addr_OUT(mem_addr_1_addr_out));
  valE_Send vale_send_1 (.valE_IN(alu_1_alu_out), .enable(EXECUTE_ENABLE), .valE_OUT(vale_send_1_vale_out));
  alu alu_1 (
    .ALU_A(alu_a_logic_1_alu_a_out), .ALU_B(main_1_alu_b_out), .FLAG(alu_1_flag), .ALU_OUT(alu_1_alu_out),
    .ALU_fun(instruction_memory_1_ifun));
  ALU_A_Logic alu_a_logic_1 (
    .valA_IN(vala_valb_send_1_vala_out), .valC_IN(instruction_memory_1_valc),
    .ICODE(instruction_memory_1_icode), .ALU_A_OUT(alu_a_logic_1_alu_a_out));
  // Probe on RAM_ADDR
  Memory_Data_Logic memory_data_logic_1 (
    .valA_IN(vala_valb_send_1_vala_out), .ICODE(instruction_memory_1_icode),
    .ALU_A_OUT(memory_data_logic_1_alu_a_out));
  alu_b_logic_main main_1 (
    .valB_IN(vala_valb_send_1_valb_out), .ICODE(instruction_memory_1_icode), .ALU_B_OUT(main_1_alu_b_out));
  _6x8_Register_File u_6x8_register_file_1 (
    .INPUT_0(valm_send_1_valm_8_out), .INPUT_1(vale_send_1_vale_out), .W_Port_0(reg_write_sel_dstem_1_dstm),
    .W_Port_1(reg_write_sel_dstem_1_dste), .W_Enable_0(and_2_out), .W_Enable_1(and_3_out),
    .OUTPUT_0(n6x8_register_file_1_output_0), .OUTPUT_1(n6x8_register_file_1_output_1),
    .Read_Port_0(reg_read_sel_logic_1_ra_out), .Read_Port_1(reg_read_sel_logic_1_r_b_out),
    .R_Enable_0(and_4_out), .R_Enable_1(and_5_out));
  reg_read_sel_logic reg_read_sel_logic_1 (
    .rA_IN(instruction_memory_1_ra), .ICODE_IN(instruction_memory_1_icode), .rB_IN(instruction_memory_1_rb),
    .rA_OUT(reg_read_sel_logic_1_ra_out), .r_B_OUT(reg_read_sel_logic_1_r_b_out));
  assign bit_extender_1_out = {{16{1'b0}}, memory_data_logic_1_alu_a_out};  // Bit_Extender bit_extender_1
  // Probe on vale_send_1_vale_out
  // Probe on main_1_alu_b_out
  and and_4 (and_4_out, register_read_logic_1_ra_enable, DECODE_ENABLE);
  and and_5 (and_5_out, register_read_logic_1_rb_enable, DECODE_ENABLE);
  Clock clock_2 (.out(clock_2_out));
  memory_controller memory_controller_1 (
    .write_enable(memory_controller_1_write_enable), .icode(instruction_memory_1_icode),
    .canwrite(MEMORY_ENABLE));  // open: read_enable
  assign RAM_STORE_ENABLE = not_1_out ? memory_controller_1_write_enable : 1'bz;  // Controlled_Buffer controlled_buffer_5
  assign RAM_DATA_IN = MEMORY_ENABLE ? bit_extender_1_out : 24'bz;  // Controlled_Buffer controlled_buffer_6
  // Probe on RAM_DATA_IN
  // Probe on vala_valb_send_1_vala_out
  valA_valB_Send vala_valb_send_1 (
    .valA_in(n6x8_register_file_1_output_0), .valB_in(n6x8_register_file_1_output_1),
    .valA_out(vala_valb_send_1_vala_out), .valB_out(vala_valb_send_1_valb_out), .enable(DECODE_ENABLE));
  // Probe on RAM_DATA_OUT
  RAM #(.dataWidth(24), .bus("separate")) ram_1 (
    .addr(RAM_ADDR), .din(RAM_DATA_IN), .data(RAM_DATA_OUT), .str(RAM_STORE_ENABLE), .clk(clock_2_out),
    .ld(RAM_LOAD_ENABLE));  // open: sel, clr
  assign RAM_LOAD_ENABLE = not_1_out ? 1'b1 : 1'bz;  // Controlled_Buffer controlled_buffer_7
  valM_Send valm_send_1 (
    .valM_IN(RAM_DATA_OUT), .enable(MEMORY_ENABLE), .valM_24_OUT(valm_send_1_valm_24_out),
    .valM_8_OUT(valm_send_1_valm_8_out));
  register_read_logic register_read_logic_1 (
    .rA_Enable(register_read_logic_1_ra_enable), .rB_Enable(register_read_logic_1_rb_enable),
    .icode(instruction_memory_1_icode));
  // Probe on valm_send_1_valm_8_out
  // Probe on instruction_memory_1_icode

  // Notes on the sheet:
  //   m
  //   e
endmodule

module instruction_memory (
  input  [23:0] ramdata_IN,
  input  ENABLE,
  input  [7:0] NEWPC,
  output [3:0] ICODE,
  output [3:0] IFUN,
  output [3:0] rA,
  output [3:0] rB,
  output [7:0] valC,
  output [7:0] ramaddr_OUT,
  output [7:0] PC
);

  wire clock_1_out;

  Register u_pc (.D(NEWPC), .en(ENABLE), .Q(PC), .clk(clock_1_out));  // open: clr
  Clock clock_1 (.out(clock_1_out));
  Register #(.width(24)) code (
    .D(ramdata_IN), .en(ENABLE), .Q({ICODE, IFUN, rA, rB, valC}), .clk(clock_1_out));  // open: clr

  assign ramaddr_OUT = PC;

  // Notes on the sheet:
  //   ENABLE: pull=down
endmodule

module register_read_logic (
  input  [3:0] icode,
  output rA_Enable,
  output rB_Enable
);

  wire and_1_out, and_2_out, and_3_out, and_4_out, and_5_out, and_6_out, and_7_out, not_1_out, not_2_out,
       not_3_out, not_4_out, not_5_out, not_6_out, not_7_out, not_8_out, not_9_out, not_10_out, not_11_out,
       not_13_out, not_14_out, not_15_out;
  wire [3:0] undriven;

  Multiplexer #(.select(4), .disabled(0), .enable("false")) multiplexer_1 (
    .in0(1'b1), .in1(1'b0), .in2(1'b0), .in3(1'b0), .in4(1'b0), .in5(1'b1), .in6(1'b0), .in7(1'b0),
    .in8(1'b0), .in9(1'b0), .in10(1'b0), .in11(1'b1), .in12(1'b0), .in13(1'b0), .in14(1'b1), .out(rA_Enable),
    .sel(icode));  // open: in15
  Multiplexer #(.select(4), .disabled(0), .enable("false")) multiplexer_2 (
    .in0(1'b1), .in1(1'b0), .in2(1'b0), .in3(1'b0), .in4(1'b1), .in5(1'b1), .in6(1'b1), .in7(1'b0),
    .in8(1'b0), .in9(1'b0), .in10(1'b0), .in11(1'b1), .in12(1'b1), .in13(1'b1), .in14(1'b1), .out(rB_Enable),
    .sel(icode));  // open: in15
  not not_1 (not_1_out, undriven[3]);
  not not_2 (not_2_out, undriven[1]);
  not not_3 (not_3_out, undriven[0]);
  not not_4 (not_4_out, undriven[1]);
  not not_5 (not_5_out, undriven[0]);
  not not_6 (not_6_out, undriven[3]);
  not not_7 (not_7_out, undriven[2]);
  not not_8 (not_8_out, undriven[3]);
  and and_1 (and_1_out, not_8_out, not_9_out, not_10_out);
  not not_9 (not_9_out, undriven[1]);
  not not_10 (not_10_out, undriven[0]);
  not not_11 (not_11_out, undriven[3]);
  not not_12 (not_11_out, undriven[3]);
  and and_2 (and_2_out, not_11_out, undriven[2], not_13_out);
  not not_13 (not_13_out, undriven[1]);
  not not_14 (not_14_out, undriven[3]);
  and and_3 (and_3_out, not_14_out, undriven[2], not_15_out);
  not not_15 (not_15_out, undriven[0]);
  and and_4 (and_4_out, not_1_out, not_2_out, not_3_out);
  and and_5 (and_5_out, undriven[2], not_4_out, not_5_out);
  and and_6 (and_6_out, not_6_out, undriven[2], undriven[0]);
  and and_7 (and_7_out, undriven[3], not_7_out, undriven[1], undriven[0]);
  // OR_Gate or_1 has open pins: in0=and_1_out, in1=and_2_out, in2=and_3_out, out=open
  // OR_Gate or_2 has open pins: in0=and_4_out, in1=and_5_out, in2=and_6_out, in3=and_7_out, out=open
endmodule

module valA_valB_Send (
  input  [7:0] valA_in,
  input  [7:0] valB_in,
  input  enable,
  output [7:0] valA_out,
  output [7:0] valB_out
);

  wire clock_1_out, undriven, undriven_2;

  Clock clock_1 (.out(clock_1_out));
  Register register_1 (.D(valA_in), .en(enable), .Q(valA_out), .clk(clock_1_out), .clr(undriven));
  Register register_2 (.D(valA_in), .en(enable), .Q(valA_out), .clk(clock_1_out), .clr(undriven));
  Register register_3 (.D(valB_in), .en(enable), .Q(valB_out), .clk(clock_1_out), .clr(undriven_2));
  Register register_4 (.D(valB_in), .en(enable), .Q(valB_out), .clk(clock_1_out), .clr(undriven_2));
endmodule

module valE_Send (
  input  [7:0] valE_IN,
  input  enable,
  output [7:0] valE_OUT
);

  wire clock_1_out;

  Clock clock_1 (.out(clock_1_out));
  Register register_1 (.D(valE_IN), .en(enable), .Q(valE_OUT), .clk(clock_1_out));  // open: clr
endmodule

module valM_Send (
  input  [23:0] valM_IN,
  input  enable,
  output [23:0] valM_24_OUT,
  output [7:0] valM_8_OUT
);

  wire clock_1_out;

  Register #(.width(24)) register_1 (.D(valM_IN), .en(enable), .Q(valM_24_OUT), .clk(clock_1_out));  // open: clr
  Clock clock_1 (.out(clock_1_out));
  Bit_Extender #(.in_width(24), .out_width(8)) bit_extender_1 (.in(valM_24_OUT), .out(valM_8_OUT));
endmodule
