// Logisim project alu.circ as structural Verilog: 1 circuit, main circuit alu
module alu (
  input  [7:0] ALU_A,
  input  [7:0] ALU_B,
  input  [3:0] ALU_fun,
  output [1:0] FLAG,
  output [7:0] ALU_OUT
);

  wire [7:0] adder_1_out, divider_1_out, multiplier_1_out, subtractor_1_out, subtractor_2_out;

  Adder adder_1 (.a(ALU_A), .b(ALU_B), .out(adder_1_out));  // open: cin, cout
  Subtractor subtractor_1 (.a(ALU_B), .b(ALU_A), .out(subtractor_1_out));  // open: bin, bout
  Multiplier multiplier_1 (.a(ALU_B), .b(ALU_A), .out(multiplier_1_out));  // open: cin, cout
  Divider divider_1 (.a(ALU_B), .b(ALU_A), .out(divider_1_out));  // open: upper, rem
  Subtractor subtractor_2 (.a(ALU_A), .b(ALU_B), .out(subtractor_2_out), .bout(FLAG[0]));  // open: bin
  Comparator comparator_1 (.a(ALU_OUT), .b({8{1'b0}}), .eq(FLAG[1]));  // open: gt, lt
  Multiplexer #(.select(4), .width(8), .enable("false")) multiplexer_1 (
    .in0(adder_1_out), .in1(subtractor_1_out), .in2(multiplier_1_out), .in3(divider_1_out),
    .in4(subtractor_2_out), .in14(ALU_B), .out(ALU_OUT), .sel(ALU_fun));  // open: in5, in6, in7, in8, in9, in10, in11, in12, in13, in15
endmodule
