// Logisim project alu_a_logic.circ as structural Verilog: 1 circuit, main circuit ALU_A Logic
module ALU_A_Logic (
  input  [7:0] valA_IN,
  input  [7:0] valC_IN,
  input  [3:0] ICODE,
  output [7:0] ALU_A_OUT
);

  Multiplexer #(.select(4), .width(8), .enable("false")) multiplexer_1 (
    .in0(valA_IN), .in1({8{1'b0}}), .in2({8{1'b0}}), .in3({8{1'b0}}), .in4(valC_IN), .in5(valC_IN),
    .in6({8{1'b0}}), .in7(valC_IN), .in8({8{1'b0}}), .in9({8{1'b0}}), .in10({8{1'b0}}), .in11(8'h1),
    .in12(8'h1), .in13(8'h1), .in14(valA_IN), .out(ALU_A_OUT), .sel(ICODE));  // open: in15
endmodule
