// Logisim project alu_b_logic.circ as structural Verilog: 1 circuit, main circuit main
module main (
  input  [7:0] valB_IN,
  input  [3:0] ICODE,
  output [7:0] ALU_B_OUT
);

  Multiplexer #(.select(4), .width(8), .enable("false")) multiplexer_1 (
    .in0(valB_IN), .in1({8{1'b0}}), .in2({8{1'b0}}), .in3({8{1'b0}}), .in4(valB_IN), .in5(valB_IN),
    .in6(valB_IN), .in7({8{1'b0}}), .in8({8{1'b0}}), .in9({8{1'b0}}), .in10({8{1'b0}}), .in11(valB_IN),
    .in12(valB_IN), .in13(valB_IN), .in14(valB_IN), .out(ALU_B_OUT), .sel(ICODE));  // open: in15
endmodule
