// Logisim project lab4_problem2.circ as structural Verilog: 4 circuits, main circuit main
module main (
  input  [7:0] ADDRESS_INPUT,
  input  INPUT_ENABLE,
  input  RAM_LOAD,
  input  OUTPUT_ENABLE,
  input  ROM_ENABLE,
  input  RAM_ENABLE,
  output [7:0] DATA_OUTPUT
);

  wire CLK_out, encode_1_outputram, encode_1_outputrom, not_1_out, RAM_CLEAR_out;
  wire [7:0] controlled_buffer_1_out, n8_bit_register_1_out, n8_bit_register_2_out, ram_1_data, rom_1_data;

  Clock CLK (.out(CLK_out));
  assign controlled_buffer_1_out = INPUT_ENABLE ? ADDRESS_INPUT : 8'bz;  // Controlled_Buffer controlled_buffer_1
  ENCODE encode_1 (
    .ROM_enable(ROM_ENABLE), .RAM_enable(RAM_ENABLE), .OUTPUTROM(encode_1_outputrom),
    .OUTPUTRAM(encode_1_outputram));
  ROM rom_1 (.addr(controlled_buffer_1_out), .data(rom_1_data), .sel(encode_1_outputrom));
  _8_bit_register u_8_bit_register_1 (
    .Out(n8_bit_register_1_out), .Load(encode_1_outputrom), .In(rom_1_data), .in_1(CLK_out));
  not not_1 (not_1_out, RAM_LOAD);
  Button RAM_CLEAR (.out(RAM_CLEAR_out));
  RAM #(.bus("asynch")) ram_1 (
    .addr(controlled_buffer_1_out), .data(ram_1_data), .sel(encode_1_outputram), .ld(not_1_out),
    .clr(RAM_CLEAR_out));
  assign ram_1_data = RAM_LOAD ? n8_bit_register_1_out : 8'bz;  // Controlled_Buffer controlled_buffer_2
  _8_bit_register u_8_bit_register_2 (
    .Out(n8_bit_register_2_out), .Load(encode_1_outputram), .In(ram_1_data), .in_1(CLK_out));
  assign DATA_OUTPUT = OUTPUT_ENABLE ? n8_bit_register_2_out : 8'bz;  // Controlled_Buffer controlled_buffer_3

  // Notes on the sheet:
  //   contents of rom_1 (hex, n*v repeats v):
  //   0 1 2 3 4 5 6 7 8 9 a b c d e f 10 11 12 13 14 15 16 17 18 19 1a 1b 1c 1d 1e 1f 20 21 22 23 24 25 26
  //   27 28 29 2a 2b 2c 2d 2e 2f 30 31 32 33 34 35 36 37 38 39 3a 3b 3c 3d 3e 3f 40 41 42 43 44 45 46 47
  //   48 49 4a 4b 4c 4d 4e 4f 50 51 52 53 54 55 56 57 58 59 5a 5b 5c 5d 5e 5f 60 61 62 63 64 65 66 67 68
  //   69 6a 6b 6c 6d 6e 6f 70 71 72 73 74 75 76 77 78 79 7a 7b 7c 7d 7e 7f 80 81 82 83 84 85 86 87 88 89
  //   8a 8b 8c 8d 8e 8f 90 91 92 93 94 95 96 97 98 99 9a 9b 9c 9d 9e 9f a0 a1 a2 a3 a4 a5 a6 a7 a8 a9 aa
  //   ab ac ad ae af b0 b1 b2 b3 b4 b5 b6 b7 b8 b9 ba bb bc bd be bf c0 c1 c2 c3 c4 c5 c6 c7 c8 c9 ca cb
  //   cc cd ce cf d0 d1 d2 d3 d4 d5 d6 d7 d8 d9 da db dc dd de df e0 e1 e2 e3 e4 e5 e6 e7 e8 e9 ea eb ec
  //   ed ee ef f0 f1 f2 f3 f4 f5 f6 f7 f8 f9 fa fb fc fd fe ff
endmodule

module _8_bit_register (
  input  in_1,
  input  Load,
  input  [7:0] In,
  output [7:0] Out
);

  wire multiplexer_1_out, multiplexer_2_out, multiplexer_3_out, multiplexer_4_out, multiplexer_5_out,
       multiplexer_6_out, multiplexer_7_out, multiplexer_8_out;

  Multiplexer #(.enable("false")) multiplexer_1 (.in0(Out[0]), .in1(In[0]), .out(multiplexer_1_out), .sel(Load));
  Dflipflop dflipflop_1 (.D(multiplexer_1_out), .Clk(in_1), .Q(Out[0]));
  Multiplexer #(.enable("false")) multiplexer_2 (.in0(Out[1]), .in1(In[1]), .out(multiplexer_2_out), .sel(Load));
  Dflipflop dflipflop_2 (.D(multiplexer_2_out), .Clk(in_1), .Q(Out[1]));
  Multiplexer #(.enable("false")) multiplexer_3 (.in0(Out[2]), .in1(In[2]), .out(multiplexer_3_out), .sel(Load));
  Dflipflop dflipflop_3 (.D(multiplexer_3_out), .Clk(in_1), .Q(Out[2]));
  Multiplexer #(.enable("false")) multiplexer_4 (.in0(Out[3]), .in1(In[3]), .out(multiplexer_4_out), .sel(Load));
  Dflipflop dflipflop_4 (.D(multiplexer_4_out), .Clk(in_1), .Q(Out[3]));
  Multiplexer #(.enable("false")) multiplexer_5 (.in0(Out[4]), .in1(In[4]), .out(multiplexer_5_out), .sel(Load));
  Dflipflop dflipflop_5 (.D(multiplexer_5_out), .Clk(in_1), .Q(Out[4]));
  Multiplexer #(.enable("false")) multiplexer_6 (.in0(Out[5]), .in1(In[5]), .out(multiplexer_6_out), .sel(Load));
  Dflipflop dflipflop_6 (.D(multiplexer_6_out), .Clk(in_1), .Q(Out[5]));
  Multiplexer #(.enable("false")) multiplexer_7 (.in0(Out[6]), .in1(In[6]), .out(multiplexer_7_out), .sel(Load));
  Dflipflop dflipflop_7 (.D(multiplexer_7_out), .Clk(in_1), .Q(Out[6]));
  Multiplexer #(.enable("false")) multiplexer_8 (.in0(Out[7]), .in1(In[7]), .out(multiplexer_8_out), .sel(Load));
  Dflipflop dflipflop_8 (.D(multiplexer_8_out), .Clk(in_1), .Q(Out[7]));

  // Notes on the sheet:
  //   Out: pull=down
endmodule

module Dflipflop (
  input  D,
  input  Clk,
  output Q
);

  wire and_1_out, and_2_out, and_3_out, and_4_out, nor_1_out, nor_2_out, nor_3_out, not_1_out, not_2_out,
       not_3_out;

  not not_1 (not_1_out, Clk);
  not not_2 (not_2_out, D);
  and and_1 (and_1_out, D, not_1_out);
  and and_2 (and_2_out, not_1_out, not_2_out);
  nor nor_1 (nor_1_out, and_1_out, nor_2_out);
  nor nor_2 (nor_2_out, nor_1_out, and_2_out);
  not not_3 (not_3_out, nor_2_out);
  and and_3 (and_3_out, nor_2_out, Clk);
  and and_4 (and_4_out, Clk, not_3_out);
  nor nor_3 (nor_3_out, and_3_out, Q);
  nor nor_4 (Q, nor_3_out, and_4_out);

  // Notes on the sheet:
  //   Q: pull=down
  //   74x04 Pin 1A-1Y
  //   74x04 Pin 2A-2Y
  //   74x08 Pins 1A,1B-1Y
  //   74x08 Pins 2A,2B-2Y
  //   74x32 Pins 1A,1B-1Y
  //   74x32 Pins 2A,2B-2Y
  //   74x04 Pin 3A-3Y
  //   74x08 Pins 3A,3B-3Y
  //   74x08 Pins 4A,4B-4Y
  //   74x32 Pins 3A,3B-3Y
  //   74x32 Pins 4A,4B-4Y
endmodule

module ENCODE (
  input  ROM_enable,
  input  RAM_enable,
  output OUTPUTROM,
  output OUTPUTRAM
);

  wire not_1_out, not_2_out;

  not not_1 (not_1_out, RAM_enable);
  not not_2 (not_2_out, ROM_enable);
  and and_1 (OUTPUTROM, ROM_enable, not_1_out);
  and and_2 (OUTPUTRAM, not_2_out, RAM_enable);
endmodule
