// Logisim project mem_addr_logic.circ as structural Verilog: 1 circuit, main circuit mem_addr
module mem_addr (
  input  [7:0] valA_IN,
  input  [7:0] valE_IN,
  input  [3:0] ICODE,
  output [7:0] Addr_OUT
);

  Multiplexer #(.select(4), .width(8), .enable("false")) multiplexer_1 (
    .in4(valE_IN), .in5(valE_IN), .in11(valE_IN), .in12(valA_IN), .in13(valA_IN), .in14(valA_IN),
    .out(Addr_OUT), .sel(ICODE));  // open: in0, in1, in2, in3, in6, in7, in8, in9, in10, in15
endmodule
