// Logisim project memory_control.circ as structural Verilog: 1 circuit, main circuit memory_controller
module memory_controller (
  input  [3:0] icode,
  input  canwrite,
  output read_enable,
  output write_enable
);

  wire and_1_out, and_2_out, and_3_out, and_4_out, and_5_out, and_6_out, not_1_out, not_2_out, not_3_out,
       not_4_out, not_5_out, not_6_out, not_7_out, not_8_out, not_9_out;
  wire [3:0] undriven;

  Multiplexer #(.select(4), .disabled(0), .enable("false")) multiplexer_1 (
    .in0(1'b1), .in1(1'b1), .in2(1'b1), .in3(1'b1), .in4(1'b1), .in5(1'b0), .in6(1'b1), .in7(1'b1),
    .in8(1'b1), .in9(1'b1), .in10(1'b1), .in11(1'b0), .in12(1'b1), .in13(1'b1), .in14(1'b0), .in15(1'b1),
    .out(read_enable), .sel(icode));
  not not_1 (not_1_out, undriven[3]);
  not not_2 (not_2_out, undriven[2]);
  not not_3 (not_3_out, undriven[2]);
  not not_4 (not_4_out, undriven[2]);
  not not_5 (not_5_out, undriven[3]);
  not not_6 (not_6_out, undriven[2]);
  not not_7 (not_7_out, undriven[1]);
  not not_8 (not_8_out, undriven[0]);
  and and_1 (and_1_out, not_1_out, not_2_out);
  and and_2 (and_2_out, not_3_out, undriven[0]);
  and and_3 (and_3_out, not_4_out, undriven[1]);
  and and_4 (and_4_out, undriven[3], undriven[2]);
  and and_5 (and_5_out, not_5_out, undriven[2]);
  and and_6 (and_6_out, undriven[3], not_6_out, not_7_out, not_8_out);
  not not_9 (not_9_out, read_enable);
  // OR_Gate or_1 has open pins: in0=and_1_out, in1=and_2_out, in2=and_3_out, in3=and_4_out, out=open
  // OR_Gate or_2 has open pins: in0=and_5_out, in1=and_6_out, out=open
  and and_7 (write_enable, not_9_out, canwrite);
endmodule
