// Logisim project pc_increment_logic.circ as structural Verilog: 1 circuit, main circuit pc_increment_jump_controller
module pc_increment_jump_controller (
  input  [3:0] ifun,
  input  [3:0] icode,
  input  [7:0] ValM,
  input  [1:0] FLAG,
  input  [7:0] PC_Increment_Counter_Value,
  input  [7:0] ValC,
  output [7:0] PC_Increment_Final_Output
);

  wire comparator_1_eq, comparator_2_eq, comparator_3_eq, or_1_out;
  wire [3:0] multiplexer_8_out;
  wire [7:0] multiplexer_1_out, multiplexer_2_out, multiplexer_3_out, multiplexer_4_out, multiplexer_5_out,
       multiplexer_6_out, multiplexer_7_out, multiplexer_9_out, subtractor_1_out;

  Multiplexer #(.select(2), .width(8), .enable("false")) multiplexer_1 (
    .in0(PC_Increment_Counter_Value), .in1(ValC), .in2(ValC), .in3(PC_Increment_Counter_Value),
    .out(multiplexer_1_out), .sel(FLAG));
  Multiplexer #(.select(4), .width(8), .enable("false")) multiplexer_2 (
    .in0(ValC), .in1(multiplexer_1_out), .in2(multiplexer_3_out), .in3(multiplexer_4_out),
    .in4(multiplexer_5_out), .in5(multiplexer_6_out), .in6(multiplexer_7_out),
    .in7(PC_Increment_Counter_Value), .in8(PC_Increment_Counter_Value), .in9(PC_Increment_Counter_Value),
    .in10(PC_Increment_Counter_Value), .in11(PC_Increment_Counter_Value), .in12(PC_Increment_Counter_Value),
    .in13(PC_Increment_Counter_Value), .in14(PC_Increment_Counter_Value), .in15(PC_Increment_Counter_Value),
    .out(multiplexer_2_out), .sel(multiplexer_8_out));
  Multiplexer #(.select(2), .width(8), .enable("false")) multiplexer_3 (
    .in0(PC_Increment_Counter_Value), .in1(ValC), .in2(PC_Increment_Counter_Value),
    .in3(PC_Increment_Counter_Value), .out(multiplexer_3_out), .sel(FLAG));
  Multiplexer #(.select(2), .width(8), .enable("false")) multiplexer_4 (
    .in0(PC_Increment_Counter_Value), .in1(PC_Increment_Counter_Value), .in2(ValC),
    .in3(PC_Increment_Counter_Value), .out(multiplexer_4_out), .sel(FLAG));
  Multiplexer #(.select(2), .width(8), .enable("false")) multiplexer_5 (
    .in0(ValC), .in1(ValC), .in2(PC_Increment_Counter_Value), .in3(PC_Increment_Counter_Value),
    .out(multiplexer_5_out), .sel(FLAG));
  Multiplexer #(.select(2), .width(8), .enable("false")) multiplexer_6 (
    .in0(ValC), .in1(PC_Increment_Counter_Value), .in2(PC_Increment_Counter_Value),
    .in3(PC_Increment_Counter_Value), .out(multiplexer_6_out), .sel(FLAG));
  Comparator #(.width(4)) comparator_1 (.a(icode), .b(4'b1010), .eq(comparator_1_eq));  // open: gt, lt
  Multiplexer #(.select(2), .width(8), .enable("false")) multiplexer_7 (
    .in0(ValC), .in1(PC_Increment_Counter_Value), .in2(ValC), .in3(PC_Increment_Counter_Value),
    .out(multiplexer_7_out), .sel(FLAG));
  Multiplexer #(.width(4), .enable("false")) multiplexer_8 (
    .in0(4'b0111), .in1(ifun), .out(multiplexer_8_out), .sel(or_1_out));
  or or_1 (or_1_out, comparator_2_eq, comparator_3_eq);
  Multiplexer #(.width(8), .enable("false")) multiplexer_9 (
    .in0(multiplexer_2_out), .in1(subtractor_1_out), .out(multiplexer_9_out), .sel(comparator_1_eq));
  Comparator #(.width(4)) comparator_2 (.a(icode), .b(4'b1101), .eq(comparator_2_eq));  // open: gt, lt
  Comparator #(.width(4)) comparator_3 (.a(icode), .b(4'b1001), .eq(comparator_3_eq));  // open: gt, lt
  Subtractor subtractor_1 (.a(PC_Increment_Counter_Value), .b(8'h2), .out(subtractor_1_out));  // open: bin, bout
  Multiplexer #(.select(4), .width(8), .enable("false")) multiplexer_10 (
    .in0(multiplexer_9_out), .in1(multiplexer_9_out), .in2(multiplexer_9_out), .in3(multiplexer_9_out),
    .in4(multiplexer_9_out), .in5(multiplexer_9_out), .in6(multiplexer_9_out), .in7(multiplexer_9_out),
    .in8(multiplexer_9_out), .in9(multiplexer_9_out), .in10(multiplexer_9_out), .in11(multiplexer_9_out),
    .in12(multiplexer_9_out), .in13(multiplexer_9_out), .in14(ValM), .out(PC_Increment_Final_Output),
    .sel(icode));  // open: in15
endmodule
