// Logisim project proto_alu.circ as structural Verilog: 1 circuit, main circuit ALU
module ALU (
  input  [7:0] INPUT_1,
  input  [7:0] INPUT_2,
  input  [1:0] FUNCTION,
  output [1:0] FLAG,
  output [7:0] OUTPUT
);

  wire [7:0] adder_1_out, demultiplexer_1_out0, demultiplexer_1_out1, demultiplexer_1_out2,
       demultiplexer_1_out3, demultiplexer_2_out0, demultiplexer_2_out1, demultiplexer_2_out2,
       demultiplexer_2_out3, divider_1_out, multiplier_1_out, subtractor_1_out;

  Demultiplexer #(.select(2), .width(8), .disabled(0), .enable("false")) demultiplexer_1 (
    .out0(demultiplexer_1_out0), .out1(demultiplexer_1_out1), .out2(demultiplexer_1_out2),
    .out3(demultiplexer_1_out3), .in(INPUT_1), .sel(FUNCTION));
  Demultiplexer #(.select(2), .width(8), .disabled(0), .enable("false")) demultiplexer_2 (
    .out0(demultiplexer_2_out0), .out1(demultiplexer_2_out1), .out2(demultiplexer_2_out2),
    .out3(demultiplexer_2_out3), .in(INPUT_2), .sel(FUNCTION));
  Comparator comparator_1 (.a(OUTPUT), .b({8{1'b0}}), .eq(FLAG[1]));  // open: gt, lt
  Adder adder_1 (.a(demultiplexer_1_out0), .b(demultiplexer_2_out0), .out(adder_1_out));  // open: cin, cout
  Subtractor subtractor_1 (
    .a(demultiplexer_1_out1), .b(demultiplexer_2_out1), .out(subtractor_1_out), .bout(FLAG[0]));  // open: bin
  Multiplier multiplier_1 (
    .a(demultiplexer_1_out2), .b(demultiplexer_2_out2), .out(multiplier_1_out));  // open: cin, cout
  Divider divider_1 (.a(demultiplexer_1_out3), .b(demultiplexer_2_out3), .out(divider_1_out));  // open: upper, rem
  assign OUTPUT = adder_1_out | subtractor_1_out | multiplier_1_out | divider_1_out;  // OR_Gate or_1, 8 bits wide
endmodule
