// Logisim project reg_read_sel.circ as structural Verilog: 1 circuit, main circuit reg_read_sel_logic
module reg_read_sel_logic (
  input  [3:0] rA_IN,
  input  [3:0] ICODE_IN,
  input  [3:0] rB_IN,
  output [3:0] rA_OUT,
  output [3:0] r_B_OUT
);

  Multiplexer #(.select(4), .width(4), .enable("false")) multiplexer_1 (
    .in0(rA_IN), .in4(rA_IN), .in5(rA_IN), .in6(rA_IN), .in7(rA_IN), .in11(rA_IN), .in12(4'b0100),
    .in14(4'b0100), .out(rA_OUT), .sel(ICODE_IN));  // open: in1, in2, in3, in8, in9, in10, in13, in15
  Multiplexer #(.select(4), .width(4), .enable("false")) multiplexer_2 (
    .in0(rB_IN), .in4(rB_IN), .in5(rB_IN), .in6(rB_IN), .in7(rB_IN), .in11(4'b0100), .in12(4'b0100),
    .in13(4'b0100), .in14(4'b0100), .out(r_B_OUT), .sel(ICODE_IN));  // open: in1, in2, in3, in8, in9, in10, in15
endmodule
