// Logisim project reg_write_sel.circ as structural Verilog: 1 circuit, main circuit reg_write_sel(dstEM)
module reg_write_sel_dstEM (
  input  [3:0] rA_IN,
  input  [3:0] rB_IN,
  input  [3:0] icode_IN,
  output [3:0] dstM,
  output [3:0] dstE
);

  Multiplexer #(.select(4), .width(4), .enable("false")) multiplexer_1 (
    .in4(rA_IN), .in12(rA_IN), .out(dstM), .sel(icode_IN));  // open: in0, in1, in2, in3, in5, in6, in7, in8, in9, in10, in11, in13, in14, in15
  Multiplexer #(.select(4), .width(4), .enable("false")) multiplexer_2 (
    .in0(rB_IN), .in6(rA_IN), .in7(rA_IN), .in11(4'b0100), .in12(4'b0100), .in14(4'b0100), .out(dstE),
    .sel(icode_IN));  // open: in1, in2, in3, in4, in5, in8, in9, in10, in13, in15
endmodule
