// Logisim project register_file.circ as structural Verilog: 1 circuit, main circuit 6x8 Register File
module _6x8_Register_File (
  input  [7:0] INPUT_0,
  input  [7:0] INPUT_1,
  input  [3:0] W_Port_0,
  input  [3:0] Read_Port_0,
  input  [3:0] W_Port_1,
  input  [3:0] Read_Port_1,
  input  W_Enable_0,
  input  R_Enable_0,
  input  W_Enable_1,
  input  R_Enable_1,
  output [7:0] OUTPUT_0,
  output [7:0] OUTPUT_1
);

  wire clock_1_out, decoder_1_out0, decoder_1_out1, decoder_1_out2, decoder_1_out3, decoder_1_out4,
       decoder_1_out5, decoder_2_out0, decoder_2_out1, decoder_2_out2, decoder_2_out3, decoder_2_out4,
       decoder_2_out5, decoder_3_out0, decoder_3_out1, decoder_3_out2, decoder_3_out3, decoder_3_out4,
       decoder_3_out5, decoder_4_out0, decoder_4_out1, decoder_4_out2, decoder_4_out3, decoder_4_out4,
       decoder_4_out5, or_1_out, or_2_out, or_3_out, or_4_out, or_5_out, or_6_out;
  wire [7:0] controlled_buffer_1_out, controlled_buffer_2_out, controlled_buffer_3_out,
       controlled_buffer_4_out, controlled_buffer_5_out, controlled_buffer_6_out, eax_q, ebx_q, ecx_q, edx_q,
       rbp_q, rsp_q;

  Decoder #(.select(4), .disabled(0)) decoder_1 (
    .out0(decoder_1_out0), .out1(decoder_1_out1), .out2(decoder_1_out2), .out3(decoder_1_out3),
    .out4(decoder_1_out4), .out5(decoder_1_out5), .sel(W_Port_0), .en(W_Enable_0));  // open: out6, out7, out8, out9, out10, out11, out12, out13, out14, out15
  Decoder #(.select(4), .disabled(0)) decoder_2 (
    .out0(decoder_2_out0), .out1(decoder_2_out1), .out2(decoder_2_out2), .out3(decoder_2_out3),
    .out4(decoder_2_out4), .out5(decoder_2_out5), .sel(W_Port_1), .en(W_Enable_1));  // open: out6, out7, out8, out9, out10, out11, out12, out13, out14, out15
  assign controlled_buffer_1_out = decoder_2_out0 ? INPUT_1 : 8'bz;  // Controlled_Buffer controlled_buffer_1
  assign controlled_buffer_2_out = decoder_2_out1 ? INPUT_1 : 8'bz;  // Controlled_Buffer controlled_buffer_2
  assign controlled_buffer_3_out = decoder_2_out2 ? INPUT_1 : 8'bz;  // Controlled_Buffer controlled_buffer_3
  assign controlled_buffer_4_out = decoder_2_out3 ? INPUT_1 : 8'bz;  // Controlled_Buffer controlled_buffer_4
  assign controlled_buffer_5_out = decoder_2_out4 ? INPUT_1 : 8'bz;  // Controlled_Buffer controlled_buffer_5
  assign controlled_buffer_6_out = decoder_2_out5 ? INPUT_1 : 8'bz;  // Controlled_Buffer controlled_buffer_6
  assign controlled_buffer_1_out = decoder_1_out0 ? INPUT_0 : 8'bz;  // Controlled_Buffer controlled_buffer_7
  assign controlled_buffer_2_out = decoder_1_out1 ? INPUT_0 : 8'bz;  // Controlled_Buffer controlled_buffer_8
  assign controlled_buffer_3_out = decoder_1_out2 ? INPUT_0 : 8'bz;  // Controlled_Buffer controlled_buffer_9
  assign controlled_buffer_4_out = decoder_1_out3 ? INPUT_0 : 8'bz;  // Controlled_Buffer controlled_buffer_10
  assign controlled_buffer_5_out = decoder_1_out4 ? INPUT_0 : 8'bz;  // Controlled_Buffer controlled_buffer_11
  assign controlled_buffer_6_out = decoder_1_out5 ? INPUT_0 : 8'bz;  // Controlled_Buffer controlled_buffer_12
  or or_1 (or_1_out, decoder_1_out0, decoder_2_out0);
  or or_2 (or_2_out, decoder_1_out1, decoder_2_out1);
  or or_3 (or_3_out, decoder_1_out2, decoder_2_out2);
  or or_4 (or_4_out, decoder_1_out3, decoder_2_out3);
  or or_5 (or_5_out, decoder_1_out4, decoder_2_out4);
  or or_6 (or_6_out, decoder_1_out5, decoder_2_out5);
  Clock clock_1 (.out(clock_1_out));
  Register eax (.D(controlled_buffer_1_out), .en(or_1_out), .Q(eax_q), .clk(clock_1_out));  // open: clr
  Register ebx (.D(controlled_buffer_2_out), .en(or_2_out), .Q(ebx_q), .clk(clock_1_out));  // open: clr
  Register ecx (.D(controlled_buffer_3_out), .en(or_3_out), .Q(ecx_q), .clk(clock_1_out));  // open: clr
  Register edx (.D(controlled_buffer_4_out), .en(or_4_out), .Q(edx_q), .clk(clock_1_out));  // open: clr
  Register rsp (.D(controlled_buffer_5_out), .en(or_5_out), .Q(rsp_q), .clk(clock_1_out));  // open: clr
  Register rbp (.D(controlled_buffer_6_out), .en(or_6_out), .Q(rbp_q), .clk(clock_1_out));  // open: clr
  // Probe on eax_q
  // Probe on ebx_q
  // Probe on ecx_q
  // Probe on edx_q
  // Probe on rsp_q
  // Probe on rbp_q
  assign OUTPUT_0 = decoder_3_out0 ? eax_q : 8'bz;  // Controlled_Buffer controlled_buffer_13
  assign OUTPUT_0 = decoder_3_out1 ? ebx_q : 8'bz;  // Controlled_Buffer controlled_buffer_14
  assign OUTPUT_0 = decoder_3_out2 ? ecx_q : 8'bz;  // Controlled_Buffer controlled_buffer_15
  assign OUTPUT_0 = decoder_3_out3 ? edx_q : 8'bz;  // Controlled_Buffer controlled_buffer_16
  assign OUTPUT_0 = decoder_3_out4 ? rsp_q : 8'bz;  // Controlled_Buffer controlled_buffer_17
  assign OUTPUT_0 = decoder_3_out5 ? rbp_q : 8'bz;  // Controlled_Buffer controlled_buffer_18
  assign OUTPUT_1 = decoder_4_out0 ? eax_q : 8'bz;  // Controlled_Buffer controlled_buffer_19
  assign OUTPUT_1 = decoder_4_out1 ? ebx_q : 8'bz;  // Controlled_Buffer controlled_buffer_20
  assign OUTPUT_1 = decoder_4_out2 ? ecx_q : 8'bz;  // Controlled_Buffer controlled_buffer_21
  assign OUTPUT_1 = decoder_4_out3 ? edx_q : 8'bz;  // Controlled_Buffer controlled_buffer_22
  assign OUTPUT_1 = decoder_4_out4 ? rsp_q : 8'bz;  // Controlled_Buffer controlled_buffer_23
  assign OUTPUT_1 = decoder_4_out5 ? rbp_q : 8'bz;  // Controlled_Buffer controlled_buffer_24
  Decoder #(.select(4), .disabled(0)) decoder_3 (
    .out0(decoder_3_out0), .out1(decoder_3_out1), .out2(decoder_3_out2), .out3(decoder_3_out3),
    .out4(decoder_3_out4), .out5(decoder_3_out5), .sel(Read_Port_0), .en(R_Enable_0));  // open: out6, out7, out8, out9, out10, out11, out12, out13, out14, out15
  Decoder #(.select(4), .disabled(0)) decoder_4 (
    .out0(decoder_4_out0), .out1(decoder_4_out1), .out2(decoder_4_out2), .out3(decoder_4_out3),
    .out4(decoder_4_out4), .out5(decoder_4_out5), .sel(Read_Port_1), .en(R_Enable_1));  // open: out6, out7, out8, out9, out10, out11, out12, out13, out14, out15

  // Notes on the sheet:
  //   DEBUG Probes
endmodule
